# Fritzing sketch ESP32-button-sw (saved by Fritzing 0.9.3b)
breadboards: 1

parts:
  Mod1 = Elecrow ESP32S WiFi/BLE Board V1.0 [part_number=ARS01119B]
  S1 = Pushbutton [package="[THT]"]
  R1 = Resistor [tolerance=±5% resistance=10k package=THT]
  LED1 = LED - 5mm [color="Red (633nm)" package="5 mm [THT]"]
  R2 = Resistor [tolerance=±5% resistance=220 package=THT]

nets:
  N1: Mod1.pin5, LED1.anode
  N2: Mod1.pin12, S1.Pin_1, S1.Pin_2, R1.Pin_1
  N3: Mod1.pin19, S1.Pin_4, R2.Pin_0
  N4: Mod1.pin38, R1.Pin_0
  N5: LED1.cathode, R2.Pin_1

notes:
  按鈕控制LED燈
  1. ESP32
  2. LED * 1
  3. button * 1
  4. 10k(棕黑橙)歐姆電阻
  5. 220(紅紅棕)歐姆電阻
  6. 杜邦線

custom parts:
  Elecrow ESP32S WiFi/BLE Board V1.0: The Elecrow ESP32S WiFi BLE Board V1.0 is one of the development boards created by Elecrow to evaluate the ESP-WROOM-32 module. It is based on the ESP32 microcontroller that boasts WiFi, Bluetooth, Ethernet and Low Power support all in a single chip. This board is 38 pins long (2x19) and 10 pins wide. Note in pcb view the mounting holes (2.8mm diameter) are only shown on silkscreen. If you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
