# Fritzing sketch esp32-mpu6050 (saved by Fritzing 0.9.3b)
breadboards: 1

parts:
  Mod1 = Elecrow ESP32S WiFi/BLE Board V1.0 [part_number=ARS01119B]
  GY1 = MPU-6050 Board GY-521 [form="♀ (female)" package=THT]
  S1 = Pushbutton [package=THT]
  S2 = Pushbutton [package=THT]

nets:
  N1: Mod1.pin13, Mod1.pin19, GY1.pin2, S1.leg0, S2.leg0
  N2: Mod1.pin35, S1.leg1
  N3: Mod1.pin36, S2.leg1
  N4: Mod1.pin38, GY1.pin1

custom parts:
  Elecrow ESP32S WiFi/BLE Board V1.0: The Elecrow ESP32S WiFi BLE Board V1.0 is one of the development boards created by Elecrow to evaluate the ESP-WROOM-32 module. It is based on the ESP32 microcontroller that boasts WiFi, Bluetooth, Ethernet and Low Power support all in a single chip. This board is 38 pins long (2x19) and 10 pins wide. Note in pcb view the mounting holes (2.8mm diameter) are only shown on silkscreen. If you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
  MPU-6050 Board GY-521: Acelerometro y Giroscopio MPU-6050 Board GY-521
