# Fritzing sketch esp32s-rc (saved by Fritzing 0.9.3b)
breadboards: 1

parts:
  Mod1 = Elecrow ESP32S WiFi/BLE Board V1.0 [part_number=ARS01119B]
  S1 = Pushbutton [package="[THT]"]
  R1 = Resistor [tolerance=±5% resistance=10k package=THT]
  C1 = Electrolytic Capacitor [capacitance=0.22mF package="100 mil [THT, electrolytic]"]

nets:
  N1: Mod1.pin13, Mod1.pin19, Mod1.pin33, C1.+
  N2: Mod1.pin20, S1.Pin_2
  N3: Mod1.pin22, R1.Pin_0, C1.-

notes:
  按鈕
  10k歐姆
  2200uF電容 pin 36 (ADC)

custom parts:
  Elecrow ESP32S WiFi/BLE Board V1.0: The Elecrow ESP32S WiFi BLE Board V1.0 is one of the development boards created by Elecrow to evaluate the ESP-WROOM-32 module. It is based on the ESP32 microcontroller that boasts WiFi, Bluetooth, Ethernet and Low Power support all in a single chip. This board is 38 pins long (2x19) and 10 pins wide. Note in pcb view the mounting holes (2.8mm diameter) are only shown on silkscreen. If you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
