# Fritzing sketch ESP32S-DHT11 (saved by Fritzing 0.9.3b)
breadboards: 1

parts:
  DHT2 = DHT11 Humitidy and Temperature Sensor
  Mod1 = Elecrow ESP32S WiFi/BLE Board V1.0 [part_number=ARS01119B]

nets:
  N1: DHT2.VDD, Mod1.pin38
  N2: DHT2.DATA, Mod1.pin34
  N3: DHT2.GND, Mod1.pin19, Mod1.pin33

custom parts:
  DHT11 Humitidy and Temperature Sensor: DHT11 Humidity and Temperature Sensor
  Elecrow ESP32S WiFi/BLE Board V1.0: The Elecrow ESP32S WiFi BLE Board V1.0 is one of the development boards created by Elecrow to evaluate the ESP-WROOM-32 module. It is based on the ESP32 microcontroller that boasts WiFi, Bluetooth, Ethernet and Low Power support all in a single chip. This board is 38 pins long (2x19) and 10 pins wide. Note in pcb view the mounting holes (2.8mm diameter) are only shown on silkscreen. If you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
