# Fritzing sketch lab-vocalctl (saved by Fritzing 0.9.3b)
breadboards: 1

parts:
  MIC2 = Microphone
  U2 = ESP32-38PinWide [part_number=ESP32-38PinWide]
  S2 = Pushbutton [package="[THT]"]
  J2 = Piezo Speaker
  X1 = USB Connectors [package=usb-microb]
  Q1 = NPN-Transistor [package="TO92 [THT]"]
  R1 = Resistor [tolerance=±5% resistance=1k package=THT]

nets:
  N1: MIC2.pin1, U2.GND, S2.Pin_1, S2.Pin_2, J2.pin1, Q1.E
  N2: MIC2.pin2, U2.GPIO36
  N3: U2.GPIO25, R1.Pin_0
  N4: U2.GPIO12, S2.Pin_3, S2.Pin_4
  N5: U2.VIN, X1.VBUS
  N6: X1.GND, Q1.C
  N7: Q1.B, R1.Pin_1

notes:
  聲音感測模組 ADC(36)
  按鈕 Pin(12)
  小喇叭 Pin(14)
  USB header
  2N2222 電晶體
  1k歐姆電阻
  LED 牙刷型照明燈

custom parts:
  ESP32-38PinWide: Generic 38-Pin ESP32 with wide format (only access to one side of pins on a breadboard) based on Stephen Lilley's HiLetgo ESP-WROOM-32 ESP32 ESP-32S Development Board.
