# Fritzing sketch lab-voice (saved by Fritzing 0.9.3b)
breadboards: 1

parts:
  MIC1 = Microphone
  U1 = ESP32-38PinWide [part_number=ESP32-38PinWide]
  S1 = Pushbutton [package="[THT]"]
  J1 = Piezo Speaker

nets:
  N1: MIC1.pin1, U1.GND, S1.Pin_1, S1.Pin_2, J1.pin1
  N2: MIC1.pin2, U1.GPIO36
  N3: U1.GPIO12, S1.Pin_3, S1.Pin_4

notes:
  聲音感測模組 ADC(36)
  按鈕 Pin(12)
  小喇叭 Pin(14)

custom parts:
  ESP32-38PinWide: Generic 38-Pin ESP32 with wide format (only access to one side of pins on a breadboard) based on Stephen Lilley's HiLetgo ESP-WROOM-32 ESP32 ESP-32S Development Board.
