# Fritzing sketch ESP32-INOUT (saved by Fritzing 0.9.3b)
breadboards: 1

parts:
  U1 = ESP32-38PinWide [part_number=ESP32-38PinWide]
  R1 = Resistor [tolerance=±5% resistance=220 package=THT]
  LED1 = LED - 5mm [color="Red (633nm)" package="5 mm [THT]"]
  LED2 = LED - 5mm [color="Green (560nm)" package="5 mm [THT]"]
  R2 = Resistor [tolerance=±5% resistance=220 package=THT]
  S1 = Pushbutton [package="[THT]"]
  R3 = Resistor [tolerance=±5% resistance=1k package=THT]

nets:
  N1: U1.VIN, S1.Pin_3, S1.Pin_4
  N2: U1.GPIO17, S1.Pin_1, S1.Pin_2, R3.Pin_0
  N3: U1.GPIO18, LED2.anode
  N4: U1.GPIO19, LED1.anode
  N5: U1.GND, R1.Pin_0, R2.Pin_0, R3.Pin_1
  N6: LED2.cathode, R2.Pin_1

custom parts:
  ESP32-38PinWide: Generic 38-Pin ESP32 with wide format (only access to one side of pins on a breadboard) based on Stephen Lilley's HiLetgo ESP-WROOM-32 ESP32 ESP-32S Development Board.
